# Fritzing sketch SimpleFOC Sensor PCB (saved by Fritzing 0.9.8b)
circuit board: 3.8cm x 1.6cm
circuit board: 2.54cm x 1.78cm
circuit board: 6.86cm x 5.33cm
circuit board: 2.54cm x 1.78cm
breadboards: 1

parts:
  J1 = female pin header, 10 pins [form="♀ (female)"]
  J2 = female pin header, 8 pins [form="♀ (female)"]
  J5 = female pin header, 8 pins [form="♀ (female)"]
  J4 = female pin header, 6 pins [form="♀ (female)"]
  J7 = female pin header, 5 pins [form="♀ (female)"]  # not connected
  J10 = female pin header, 4 pins [form="♀ (female)"]
  J11 = female pin header, 8 pins [form="♀ (female)"]
  J13 = female pin header, 8 pins [form="♀ (female)"]
  J14 = female pin header, 6 pins [form="♀ (female)"]
  J12 = female pin header, 10 pins [form="♀ (female)"]
  J6 = female pin header, 9 pins [form="♀ (female)"]
  J19 = female pin header, 3 pins [form="♀ (female)"]
  J3 = double row female pin header, 4 pins [form="♀ (female)"]
  J21 = female pin header, 5 pins [form="♀ (female)"]
  J22 = female pin header, 4 pins [form="♀ (female)"]
  J9 = female pin header, 6 pins [form="♀ (female)"]
  J8 = female pin header, 6 pins [form="♀ (female)"]
  J20 = female pin header, 4 pins [form="♀ (female)"]
  J23 = female pin header, 3 pins [form="♀ (female)"]

nets:
  N1: J1.pin1, J12.pin10
  N2: J1.pin2, J12.pin9
  N3: J1.pin3, J12.pin8
  N4: J1.pin4, J12.pin7
  N5: J1.pin5, J12.pin6
  N6: J1.pin6, J12.pin5
  N7: J1.pin7, J12.pin4
  N8: J1.pin8, J12.pin3
  N9: J1.pin9, J12.pin2, J8.pin2
  N10: J1.pin10, J12.pin1
  N11: J2.pin1, J11.pin8, J6.pin3
  N12: J2.pin2, J11.pin7
  N13: J2.pin3, J11.pin6
  N14: J2.pin4, J11.pin5, J21.pin3
  N15: J2.pin5, J11.pin4, J21.pin2
  N16: J2.pin6, J11.pin3, J21.pin1
  N17: J2.pin7, J10.pin1, J11.pin2
  N18: J2.pin8, J10.pin2, J11.pin1
  N19: J5.pin1, J13.pin8
  N20: J5.pin2, J13.pin7
  N21: J5.pin3, J13.pin6
  N22: J5.pin4, J13.pin5, J6.pin8, J21.pin5, J9.pin5
  N23: J5.pin5, J10.pin4, J13.pin4
  N24: J5.pin6, J5.pin7, J10.pin3, J13.pin2, J13.pin3, J6.pin7, J21.pin4, J9.pin4
  N25: J5.pin8, J13.pin1, J22.pin1, J20.pin1
  N26: J4.pin1, J14.pin6
  N27: J4.pin2, J14.pin5
  N28: J4.pin3, J14.pin4
  N29: J4.pin4, J14.pin3
  N30: J4.pin5, J14.pin2, J22.pin3, J20.pin3
  N31: J4.pin6, J14.pin1, J22.pin4, J20.pin4
  N32: J6.pin4, J19.pin1, J3.pin3, J8.pin6
  N33: J6.pin5, J19.pin3, J3.pin1, J9.pin2
  N34: J6.pin6, J19.pin2, J3.pin4, J9.pin3
  N35: J22.pin2, J20.pin2, J23.pin2

notes:
  ISM330DHCX
  MISO
  MOSI
  CLK
  Bluetooth
  I
  A
  B
  Gnd
  3V
  GND
  5V
  Vin
  ICM20649
  Servo 1
  Servo 2
  100K
  1K
  SWITCHED 8V
  © Steven Gregorki 2023
  FET
  In
  8V
